# Fritzing sketch Model (saved by Fritzing 0.9.2b)
breadboards: 1

parts:
  Часть1 = Arduino Uno (Rev3)
  KY-1 = Keyes Relay [package=THT]
  KY-2 = Keyes Relay [package=THT]
  KY-3 = Keyes Relay [package=THT]
  KY-4 = Keyes Relay [package=THT]
  S2 = Reed switch [package=THT]
  S3 = Reed switch [package=THT]
  S4 = Reed switch [package=THT]

nets:
  N1: Часть1.A0, KY-1.signal
  N2: Часть1.A1, KY-2.signal
  N3: Часть1.A2, KY-3.signal
  N4: Часть1.A3, KY-4.signal
  N5: Часть1.D12/MISO, S3.pin_2
  N6: Часть1.D13/SCK, S4.pin_2
  N7: Часть1.D2, S2.pin_2
  N8: Часть1.5V, KY-1.power, S2.pin_1, S3.pin_1, S4.pin_1
  N9: Часть1.GND, KY-1.ground

notes:
  CC3000 wi-fi CS
  cc3000 led
  cc3000 vbat
  cc3000 SDCS
  cc3000 IRQ
  Прерывание от расходомера
  Низкий уровень в скважине
  Максимальный уровень в бочке

custom parts:
  Keyes Relay: The Keyes 5V relay module is suitable for SCM development, home appliance control. It uses a 5V~12V TIL control signal which can control DC / AC signal.
